// Logisim project Ex1.circ as structural Verilog: 1 circuit, main circuit main
module main (
  input  A3,
  input  A2,
  input  A1,
  input  A0,
  output O0,
  output [1:0] O1
);

  wire and_1_out, not_1_out, not_2_out, or_1_out;

  not not_1 (not_1_out, A3);
  not not_2 (not_2_out, A2);
  and and_1 (and_1_out, not_1_out, not_2_out, not_2_out);
  or or_1 (or_1_out, A1, A0);
  xnor xnor_1 (O0, and_1_out, or_1_out);

  assign O1 = {A0, A1};
endmodule
