// Logisim project Tp1.circ as structural Verilog: 8 circuits, main circuit soustracteur 8b
module additionneur_8b (
  input  in_1,
  input  in_2,
  input  in_3,
  input  in_4,
  input  in_5,
  input  in_6,
  input  in_7,
  input  in_8,
  input  in_9,
  input  in_10,
  input  in_11,
  input  in_12,
  input  in_13,
  input  in_14,
  input  in_15,
  input  in_16,
  input  in_17,
  output out_18,
  output out_19,
  output out_20,
  output out_21,
  output out_22,
  output out_23,
  output out_24,
  output out_25,
  output out_26
);

  wire additionneur_1b_2_r0, additionneur_1b_3_r0, additionneur_1b_4_r0, additionneur_1b_5_r0,
       additionneur_1b_6_r0, additionneur_1b_7_r0, additionneur_1b_8_r0;

  Additionneur_1b additionneur_1b_1 (.A(in_1), .B(in_9), .S(out_19), .R_1(additionneur_1b_3_r0), .R0(out_18));
  Additionneur_1b additionneur_1b_2 (
    .A(in_3), .B(in_11), .S(out_21), .R_1(additionneur_1b_4_r0), .R0(additionneur_1b_2_r0));
  Additionneur_1b additionneur_1b_3 (
    .A(in_2), .B(in_10), .S(out_20), .R_1(additionneur_1b_2_r0), .R0(additionneur_1b_3_r0));
  Additionneur_1b additionneur_1b_4 (
    .A(in_4), .B(in_12), .S(out_22), .R_1(additionneur_1b_5_r0), .R0(additionneur_1b_4_r0));
  Additionneur_1b additionneur_1b_5 (
    .A(in_5), .B(in_13), .S(out_23), .R_1(additionneur_1b_7_r0), .R0(additionneur_1b_5_r0));
  Additionneur_1b additionneur_1b_6 (
    .A(in_7), .B(in_15), .S(out_25), .R_1(additionneur_1b_8_r0), .R0(additionneur_1b_6_r0));
  Additionneur_1b additionneur_1b_7 (
    .A(in_6), .B(in_14), .S(out_24), .R_1(additionneur_1b_6_r0), .R0(additionneur_1b_7_r0));
  Additionneur_1b additionneur_1b_8 (.A(in_8), .B(in_16), .S(out_26), .R_1(in_17), .R0(additionneur_1b_8_r0));
endmodule

module Ex2 (
  input  A0,
  input  A1,
  input  A2,
  input  A,
  input  B,
  input  C,
  input  D,
  input  A_2,
  input  B_2,
  input  C_2,
  input  D_2,
  output O0,
  output out_13,
  output out_14
);

  wire and_1_out, and_2_out, and_5_out, and_6_out, not_1_out, not_2_out, or_1_out, or_2_out, or_3_out,
       or_4_out;

  not not_1 (not_1_out, D);
  or or_1 (or_1_out, A1, A2);
  or or_2 (or_2_out, A_2, B_2, C_2);
  and and_1 (and_1_out, C_2, not_2_out);
  not not_2 (not_2_out, D_2);
  or or_3 (or_3_out, A, B, C);
  and and_2 (and_2_out, C, not_1_out);
  and and_3 (O0, A0, or_1_out);
  and and_4 (out_13, or_3_out, and_2_out);
  and and_5 (and_5_out, or_2_out, and_1_out);
  or or_4 (or_4_out, B_2, C_2);
  and and_6 (and_6_out, A_2, or_4_out);
  and and_7 (out_14, and_5_out, and_6_out);
endmodule

module Ex3 (
  input  in_1,
  input  in_2
);

  wire and_1_out, clock_1_out, xor_1_out;

  Clock clock_1 (.out(clock_1_out));
  xor xor_1 (xor_1_out, in_1, in_2);
  and and_1 (and_1_out, xor_1_out, clock_1_out);
  LED led_1 (.in(and_1_out));
endmodule

module Additionneur_1b (
  input  R_1,
  input  A,
  input  B,
  output S,
  output R0
);

  wire and_1_out, and_2_out, xor_1_out;

  xor xor_1 (xor_1_out, A, B);
  and and_1 (and_1_out, B, A);
  or or_1 (R0, and_1_out, and_2_out);
  xor xor_2 (S, R_1, xor_1_out);
  and and_2 (and_2_out, xor_1_out, R_1);
endmodule

module Ex1 (
  input  A3,
  input  A2,
  input  A1,
  input  A0,
  output O0,
  output [1:0] O1
);

  wire and_1_out, not_1_out, not_2_out, or_1_out;

  not not_1 (not_1_out, A3);
  not not_2 (not_2_out, A2);
  and and_1 (and_1_out, not_1_out, not_2_out, not_2_out);
  or or_1 (or_1_out, A1, A0);
  xnor xnor_1 (O0, and_1_out, or_1_out);

  assign O1 = {A0, A1};
endmodule

module Demi_soustracteur (
  input  Nombre,
  input  Soustracteur,
  output S,
  output R
);

  xor xor_1 (S, Nombre, Soustracteur);
  and and_1 (R, S, Soustracteur);
endmodule

module Soustracteur_1b (
  input  Nombre,
  input  Soustracteur,
  input  R_1,
  output S,
  output R
);

  wire and_1_out, demi_soustracteur_1_r, demi_soustracteur_1_s, demi_soustracteur_2_r, demi_soustracteur_2_s;

  Demi_soustracteur demi_soustracteur_1 (
    .Nombre(Nombre), .Soustracteur(Soustracteur), .R(demi_soustracteur_1_r), .S(demi_soustracteur_1_s));
  and and_1 (and_1_out, Soustracteur, R_1);
  Demi_soustracteur demi_soustracteur_2 (
    .Nombre(demi_soustracteur_1_s), .Soustracteur(R_1), .R(demi_soustracteur_2_r), .S(demi_soustracteur_2_s));
  or or_1 (S, and_1_out, demi_soustracteur_2_s);
  or or_2 (R, demi_soustracteur_2_r, demi_soustracteur_1_r);
endmodule

module soustracteur_8b (
  input  in_1,
  input  in_2,
  input  in_3,
  input  in_4,
  input  in_5,
  input  in_6,
  input  in_7,
  input  in_8,
  input  in_9,
  input  in_10,
  input  in_11,
  input  in_12,
  input  in_13,
  input  in_14,
  input  in_15,
  input  in_16,
  input  in_17,
  output out_18,
  output out_19,
  output out_20,
  output out_21,
  output out_22,
  output out_23,
  output out_24,
  output out_25,
  output out_26
);

  wire soustracteur_1b_2_r, soustracteur_1b_3_r, soustracteur_1b_4_r, soustracteur_1b_5_r,
       soustracteur_1b_6_r, soustracteur_1b_7_r, soustracteur_1b_8_r;

  Soustracteur_1b soustracteur_1b_1 (
    .Nombre(in_1), .Soustracteur(in_9), .R_1(soustracteur_1b_3_r), .S(out_19), .R(out_18));
  Soustracteur_1b soustracteur_1b_2 (
    .Nombre(in_3), .Soustracteur(in_11), .R_1(soustracteur_1b_4_r), .S(out_21), .R(soustracteur_1b_2_r));
  Soustracteur_1b soustracteur_1b_3 (
    .Nombre(in_2), .Soustracteur(in_10), .R_1(soustracteur_1b_2_r), .S(out_20), .R(soustracteur_1b_3_r));
  Soustracteur_1b soustracteur_1b_4 (
    .Nombre(in_4), .Soustracteur(in_12), .R_1(soustracteur_1b_6_r), .S(out_22), .R(soustracteur_1b_4_r));
  Soustracteur_1b soustracteur_1b_5 (
    .Nombre(in_6), .Soustracteur(in_14), .R_1(soustracteur_1b_7_r), .S(out_24), .R(soustracteur_1b_5_r));
  Soustracteur_1b soustracteur_1b_6 (
    .Nombre(in_5), .Soustracteur(in_13), .R_1(soustracteur_1b_5_r), .S(out_23), .R(soustracteur_1b_6_r));
  Soustracteur_1b soustracteur_1b_7 (
    .Nombre(in_7), .Soustracteur(in_15), .R_1(soustracteur_1b_8_r), .S(out_25), .R(soustracteur_1b_7_r));
  Soustracteur_1b soustracteur_1b_8 (
    .Nombre(in_8), .Soustracteur(in_16), .R_1(in_17), .S(out_26), .R(soustracteur_1b_8_r));
endmodule
